# Fritzing sketch sketch (saved by Fritzing 0.9.3b)
breadboards: 1

parts:
  Part1 = Arduino Uno (Rev3)
  U1 = Sharp PC817 [package=THT]
  U2 = Sharp PC817 [package=THT]
  U3 = Sharp PC817 [package=THT]
  R1 = Resistor [tolerance=±5% resistance=330 package="0805 [SMD]"]
  R2 = Resistor [tolerance=±5% resistance=330 package="0805 [SMD]"]
  R3 = Resistor [tolerance=±5% resistance=1k package="0805 [SMD]"]
  R4 = Resistor [tolerance=±5% resistance=1k package="0805 [SMD]"]
  R5 = Resistor [tolerance=±5% resistance=1k package="0603 [SMD]"]
  JP1 = Header 2 [package=molex-1x2_lock]
  JP2 = Header 2 [package=molex-1x2_lock]
  JP3 = Header 2 [package=molex-1x2_lock]

nets:
  N1: Part1.GND, U1.Pin_3, U2.Pin_3, R5.Pin_0
  N2: Part1.D2, U3.Pin_1
  N3: Part1.D4, U2.Pin_4, R4.Pin_0
  N4: Part1.D6_PWM, U1.Pin_4, R3.Pin_0
  N5: Part1.5V, R3.Pin_1, R4.Pin_1
  N6: U1.Pin_1, JP1.1
  N7: U1.Pin_2, R1.Pin_0
  N8: U2.Pin_1, JP2.1
  N9: U2.Pin_2, R2.Pin_0
  N10: U3.Pin_2, R5.Pin_1
  N11: U3.Pin_4, JP3.1
  N12: U3.Pin_3, JP3.2
  N13: R1.Pin_1, JP1.2
  N14: R2.Pin_1, JP2.2

notes:
  Beeper
  ATX 5V
  Power Button
